# Fritzing sketch hardware_V3 (saved by Fritzing 0.8.7b)
breadboards: 1
perfboards: 2

parts:
  Componente1 = Arduino Mega 2560 (Rev3)
  Componente2 = Arduino Ethernet Shield (Rev3)
  J2 = Peltier Element
  J3 = Peltier Element
  Componente5 = EasyDriver_v44
  M1 = Stepper Motor - Bipolar
  Componente6 = EasyDriver_v44
  M2 = Stepper Motor - Bipolar
  J4 = Basic Servo
  Componente7 = SRF05 Ultrasonic Rangefinder
  Componente8 = SRF05 Ultrasonic Rangefinder
  S1 = PH meter [package=THT]
  R1 = Photocell (LDR) [package=THT]
  R3 = Resistor [tolerance=±5% resistance=100 package=THT]
  KY-1 = Keyes Relay [package=THT]
  KY-2 = Keyes Relay [package=THT]
  KY-3 = Keyes Relay [package=THT]
  KY-4 = Keyes Relay [package=THT]
  KY-5 = Keyes Relay [package=THT]
  F1 = Fan - Ventilador [package=THT]
  F2 = Fan - Ventilador [package=THT]
  F3 = Fan - Ventilador [package=THT]
  Part3 = Lilypad Battery Connect
  LED3 = LEDs [package=led10mm]
  LED4 = LEDs [package=led10mm]
  Part4 = Lilypad Battery Connect
  J7 = Generic double row female header - 10 pins [form="♀ (female)" package=THT]  # not connected
  J8 = Generic double row female header - 10 pins [form="♀ (female)" package=THT]  # not connected
  M3 = DC Motor
  JP1 = Header 1 [package=1x01_offset]  # not connected
  JP2 = Header 1 [package=1x01_offset]  # not connected
  JP3 = Header 1 [package=1x01_offset]  # not connected
  JP4 = Header 1 [package=1x01_offset]  # not connected
  JP5 = Header 1 [package=1x01_offset]  # not connected
  JP6 = Header 1 [package=1x01_offset]  # not connected
  JP7 = Header 1 [package=1x01_offset]
  JP8 = Header 1 [package=1x01_offset]  # not connected
  JP9 = Header 1 [package=1x01_offset]  # not connected
  JP10 = Header 1 [package=1x01_offset]
  JP11 = Header 1 [package=1x01_offset]
  JP12 = Header 1 [package=1x01_offset]
  JP13 = Header 1 [package=1x01_offset]
  JP14 = Header 1 [package=1x01_offset]  # not connected
  JP15 = Header 1 [package=1x01_offset]  # not connected
  JP16 = Header 1 [package=1x01_offset]  # not connected
  JP17 = Header 1 [package=1x01_offset]  # not connected
  JP18 = Header 1 [package=1x01_offset]  # not connected
  JP19 = Header 1 [package=1x01_offset]
  JP20 = Header 1 [package=1x01_offset]
  Part6 = Lilypad Battery Connect
  Componente9 = Adafruit Thermocouple Amplifier with 1-Wire Breakout Board - MAX31850K [part_number="Adafruit #1727"]
  J10 = screw terminal, 2 pins
  U1 = RELAY-SOLIDSTATE [package=relay-s108t02]
  Q2 = TIP120 Hi-Current Darlington Transistor
  Q3 = TIP120 Hi-Current Darlington Transistor
  Part7 = Lilypad Battery Connect
  U2 = RELAY-SOLIDSTATE [package=relay-s108t02]
  Part8 = Lilypad Battery Connect
  J11 = screw terminal, 2 pins
  J9 = screw terminal, 4 pins
  R4 = Resistor [tolerance=±5% resistance=100 package=THT]
  R5 = Resistor [tolerance=±5% resistance=100 package=THT]
  R6 = Resistor [tolerance=±5% resistance=100 package=THT]
  R7 = Resistor [tolerance=±5% resistance=100 package=THT]
  J12 = screw terminal, 2 pins  # not connected
  J14 = screw terminal, 2 pins  # not connected
  J16 = screw terminal, 2 pins  # not connected

nets:
  GND: Componente1.GND, J4.gnd, Componente7.GND, Componente8.GND, KY-1.power, KY-2.power, KY-3.power, KY-4.power, KY-5.power
  VCC: Componente1.5V, Componente5.VCC, Componente6.VCC, J4.vcc, Componente7.VCC, Componente8.VCC, KY-1.signal, KY-2.signal, KY-3.signal, KY-4.signal, KY-5.signal
  N1: Componente1.D22, KY-1.ground
  N2: Componente1.D26, KY-5.ground
  N3: Componente1.D30, KY-4.ground
  N4: Componente1.D34, KY-3.ground
  N5: Componente1.D38, KY-2.ground
  N6: Componente2.D8, J4.pulse
  N7: Componente2.PWM_D9, Componente8.Echo
  N8: Componente2.ETH_CS, Componente8.Trig
  GND_2: Componente2.GND, Componente5.GND, Componente6.GND, S1.pin3, R3.Pin_0, R5.Pin_0, R7.Pin_0
  N9: Componente2.A0, R1.pin_0, R3.Pin_1
  N10: Componente2.A1, S1.pin1
  N11: Componente2.A2, R6.Pin_0, R7.Pin_1
  N12: Componente2.A3, R4.Pin_0, R5.Pin_1
  N13: Componente2.D2, Componente5.STEP
  N14: Componente2.PWM_D3, Componente5.DIR
  N15: Componente2.SDCS, Componente6.STEP
  N16: Componente2.PWM_D5, Componente6.DIR
  N17: Componente2.PWM_D6, Componente7.Echo
  N18: Componente2.D7, Componente7.Trig
  N19: Componente2.5V, S1.pin2, R1.pin_1
  N20: J2.pin1, J3.pin1, F1.GND, Part4.-
  N21: J2.pin2, KY-4.NO
  N22: J3.pin2, KY-5.NO
  N23: Componente5.OUT2A, M1.B
  N24: Componente5.OUT2B, M1.A
  N25: Componente5.OUT1A, M1.C
  N26: Componente5.OUT1B, M1.D
  N27: Componente6.OUT2A, M2.B
  N28: Componente6.OUT2B, M2.A
  N29: Componente6.OUT1A, M2.C
  N30: Componente6.OUT1B, M2.D
  N31: KY-1.C, KY-2.C, Part3.+
  N32: KY-1.NO, LED4.A
  N33: KY-2.NO, LED3.A
  N34: KY-3.C, Part4.+
  N35: KY-3.NO, F1.5V
  5V: F2.5V, F3.5V, Part8.+
  N36: F2.GND, Q3.COLLECTOR
  N37: F3.GND, Q2.COLLECTOR
  N38: Part3.-, LED3.C
  N39: M3.pin_1, U1.T1
  N40: M3.pin_2, Part7.+, J11.pin1
  N41: JP7.1, Componente9.A0
  N42: JP10.1, U1.+
  N43: JP11.1, U2.+
  N44: JP12.1, Q3.BASE
  N45: JP13.1, Q2.BASE
  N46: JP19.1, Part6.+
  N47: JP20.1, Part6.-
  N48: Componente9.YELLOW+, J10.pin1
  N49: Componente9.RED-, J10.pin2
  N50: U1.T2, U2.T2
  N51: Q2.EMITTER, Q3.EMITTER
  N52: U2.T1, J11.pin2
  N53: J9.pin3, R6.Pin_1
  N54: J9.pin4, R4.Pin_1

notes:
  PERISTALTIC PUMP 1
  FISH FEEDER
  ULTRASONIC AQP
  LIGHT SENSOR
  Ph SENSOR
  240V AC power supply
  Vcc (12V) power supply
  GREENHOUSE LIGHT
  HEATER 1
  EXHAUST FAN
  AQUAPONICS LIGHT
  Ethernet
  HUMIDITY & TEMPERATURE SENSOR
  THERMOCOUPLE
  HOT FAN 1
  HOT FAN 2
  PUMP
  HEATER
  SOLID STATE RELAY
  DC DRIVER
  CONVERTER
  PLC
  RELAYS
  DRIVER 2
  DRIVER 1
  ULTRASONIC ETF
  ETHERNET
  HEATER 2

custom parts:
  Keyes Relay: The Keyes 5V relay module is suitable for SCM development, home appliance control. It uses a 5V~12V TIL control signal which can control DC / AC signal.
  Fan - Ventilador: Ventilador de 2 pines, se encuentra comunmente en computadoras de escritorio
  LEDs: LEDs Standard schematic elements and footprints for 5mm, 3mm, 1206, and 0603 sized LEDs. 5mm - Spark Fun Electronics SKU : COM-00529 (and others)
  Generic double row female header - 10 pins: Generic double row female header
  Generic double row female header - 10 pins: Generic double row female header
  Adafruit Thermocouple Amplifier with 1-Wire Breakout Board - MAX31850K: Thermocouples are very sensitive, requiring a good amplifier with a cold-compensation reference. So far we've carried the very nice MAX31855 which is an SPI interface thermocouple amplifier. The '855 is great but if you have a lot of thermocouples to measure it isn't terribly easy to use. That's why we are also carrying the new '850 model from Maxim - it's a "1-Wire" thermocouple amp which can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
